# Fritzing sketch stepping_motor_fritz (saved by Fritzing 0.9.2b)

parts:
  BeagleBone1 = BeagleBone Black
  Part1 = EasyDriver_v44
  M1 = Stepper Motor - Bipolar

nets:
  N1: BeagleBone1.no_name_yet#107, Part1.DIR
  N2: BeagleBone1.no_name_yet#108, Part1.STEP
  N3: BeagleBone1.no_name_yet#109, Part1.MS2
  N4: BeagleBone1.no_name_yet#110, Part1.MS1
  N5: BeagleBone1.no_name_yet#112, Part1.ENABLE
  N6: BeagleBone1.no_name_yet#146, Part1.GND
  N7: Part1.OUT2A, M1.A
  N8: Part1.OUT2B, M1.C
  N9: Part1.OUT1A, M1.B
  N10: Part1.OUT1B, M1.D

notes:
  12v DC

custom parts:
  BeagleBone Black: BeagleBone Black rev. A5B
